# Fritzing sketch platinemitesp8266_uQSwUOx7oS (saved by Fritzing 0.9.3b)
circuit board: 2.69259cm x 4.68858cm

parts:
  Bauteil2 = Logic Level Converter
  J1 = female pin header, 15 pins [form="♀ (female)"]
  J2 = female pin header, 15 pins [form="♀ (female)"]
  J3 = female pin header, 4 pins [form="♀ (female)"]

nets:
  N1: Bauteil2.GND, J1.pin7, J3.pin1
  N2: Bauteil2.LV, J1.pin6
  N3: Bauteil2.RX_LV, J1.pin13
  N4: Bauteil2.TX_LV, J1.pin12
  N5: Bauteil2.TX_HV, J3.pin4
  N6: Bauteil2.RX_HV, J3.pin3
  N7: Bauteil2.HV, J2.pin15, J3.pin2

notes:
  D0
  A0
  3.3V
  5V
  GND
  TX
  RX
